# Fritzing sketch fritzing_sketch (saved by Fritzing 0.9.3b)

parts:
  BAT1 = Battery Holders [package=lipo-1100mAh]
  S1 = H-Bridge with L298N
  U1 = SWITCH_SPDT [package=kps-1290]
  Onderdeel1 = Arduino Micro (Rev3)
  Onderdeel2 = SO-24x [chip_label=SO-24x package=SO(x)]  # not connected
  J1 = male pin header, 6 pins [form="♂ (male)" part_number=GND]
  J2 = male pin header, 6 pins [form="♂ (male)"]
  J3 = male pin header, 6 pins [form="♂ (male)"]
  M1 = DC Motor
  M2 = DC Motor

nets:
  N1: BAT1.+, U1.P
  GND: BAT1.-, S1.GND, Onderdeel1.GND, J1.pin6
  12V: S1.12V, U1.S, Onderdeel1.VIN
  N2: S1.ENA, Onderdeel1.D10_PWM/A10
  N3: S1.IN1, Onderdeel1.D8_PWM/A8
  N4: S1.IN2, Onderdeel1.D9_PWM/A9
  N5: S1.IN3, Onderdeel1.D5_PWM
  N6: S1.IN4, Onderdeel1.D4_PWM/A6
  N7: S1.ENB, Onderdeel1.D6_PWM/A7
  N8: S1.M1-01, M1.pin_2
  N9: S1.M1-02, M1.pin_1
  N10: S1.M2-01, M2.pin_2
  N11: S1.M2-02, M2.pin_1
  N12: Onderdeel1.RESET, J2.pin1
  N13: Onderdeel1.D2/SDA, J1.pin5
  N14: Onderdeel1.5V, J3.pin1

custom parts:
  H-Bridge with L298N: h-bridge
